// Logisim project Lab_1.circ as structural Verilog: 2 circuits, main circuit Display
module main (
  input  in_1,
  input  in_2,
  input  in_3,
  input  in_4,
  input  in_5,
  input  in_6,
  input  in_7,
  input  in_8,
  input  in_9,
  input  in_10,
  input  in_11,
  input  [7:0] in_12,
  input  in_13,
  input  in_14,
  input  in_15,
  input  in_16,
  input  in_17,
  input  in_18,
  input  in_19,
  input  in_20,
  input  in_21,
  input  in_22,
  output out_23,
  output out_24,
  output out_25,
  output out_26,
  output out_27,
  output out_28,
  output out_29,
  output out_30,
  output out_31,
  output out_32,
  output out_33,
  output out_34,
  output out_35
);

  wire and_2_out, and_3_out, binary_to_bcd_converter_1_p4, n7_segment_display_1_p1, n7_segment_display_1_p2,
       nand_1_out, nand_2_out, nand_3_out, nor_1_out, nor_2_out, nor_3_out, xor_1_out;

  and and_1 (out_23, in_1, in_3);
  or or_1 (out_26, in_6, in_10);
  not not_1 (out_30, in_15);
  LED led_1 (.in(out_23));
  LED led_2 (.in(out_26));
  LED led_3 (.in(out_30));
  nand nand_1 (nand_1_out, in_2, in_5);
  nand nand_2 (nand_2_out, in_8, in_8);
  nand nand_3 (nand_3_out, in_14, in_14);
  nand nand_4 (out_32, in_20, in_20);
  LED led_4 (.in(out_32));
  nand nand_5 (out_27, nand_2_out, nand_3_out);
  nand nand_6 (out_24, nand_1_out, nand_1_out);
  LED led_5 (.in(out_24));
  LED led_6 (.in(out_27));
  nor nor_1 (nor_1_out, in_4, in_4);
  nor nor_2 (nor_2_out, in_9, in_9);
  nor nor_3 (nor_3_out, in_16, in_18);
  nor nor_4 (out_34, in_22, in_22);
  LED led_7 (.in(out_34));
  nor nor_5 (out_25, nor_1_out, nor_2_out);
  nor nor_6 (out_31, nor_3_out, nor_3_out);
  LED led_8 (.in(out_25));
  LED led_9 (.in(out_31));
  Adder #(.width(1)) adder_1 (.a(in_11), .b(in_13), .out(out_28), .cin(in_7), .cout(out_29));
  xor xor_1 (xor_1_out, in_19, in_21);
  and and_2 (and_2_out, in_19, in_21);
  xor xor_2 (out_33, xor_1_out, in_17);
  and and_3 (and_3_out, xor_1_out, in_17);
  // BCD_to_7_Segment_decoder bcd_to_7_segment_decoder_1: pin names not known
  // _7_Segment_Display 7_segment_display_1: pin names not known; wires that end beside it: n7_segment_display_1_p1, n7_segment_display_1_p2
  // Binary_to_BCD_converter #(.binvalue(8)) binary_to_bcd_converter_1: pin names not known; wires that end beside it: in_12, n7_segment_display_1_p1, n7_segment_display_1_p2, binary_to_bcd_converter_1_p4
  or or_2 (out_35, and_3_out, and_2_out);
  // BCD_to_7_Segment_decoder bcd_to_7_segment_decoder_2: pin names not known
  // BCD_to_7_Segment_decoder bcd_to_7_segment_decoder_3: pin names not known
  // _7_Segment_Display 7_segment_display_2: pin names not known; wires that end beside it: n7_segment_display_1_p2, binary_to_bcd_converter_1_p4
  _7_Segment_Display u_7_segment_display_3 ();  // open: g, f, a, b, e, d, c, dp
endmodule

module Display (
  input  [7:0] in_1
);

  wire n7_segment_display_1_p1, n7_segment_display_1_p2, n7_segment_display_2_p2;

  // BCD_to_7_Segment_decoder bcd_to_7_segment_decoder_1: pin names not known
  // BCD_to_7_Segment_decoder bcd_to_7_segment_decoder_2: pin names not known
  // _7_Segment_Display 7_segment_display_1: pin names not known; wires that end beside it: n7_segment_display_1_p1, n7_segment_display_1_p2
  // _7_Segment_Display 7_segment_display_2: pin names not known; wires that end beside it: n7_segment_display_1_p2, n7_segment_display_2_p2
  // Binary_to_BCD_converter #(.binvalue(8)) binary_to_bcd_converter_1: pin names not known; wires that end beside it: in_1, n7_segment_display_1_p1, n7_segment_display_1_p2, n7_segment_display_2_p2
  // BCD_to_7_Segment_decoder bcd_to_7_segment_decoder_3: pin names not known
  _7_Segment_Display u_7_segment_display_3 ();  // open: g, f, a, b, e, d, c, dp
endmodule
